# Fritzing sketch wemos-d1-mini-bme280 (saved by Fritzing 0.9.9b)

parts:
  Part1 = BME280 Breakout
  WeMos_D1_Mini2 = WeMos D1 Mini

nets:
  N1: Part1.VCC, WeMos_D1_Mini2.D4
  N2: Part1.GND, WeMos_D1_Mini2.G
  N3: Part1.SCL, WeMos_D1_Mini2.D1
  N4: Part1.SDA, WeMos_D1_Mini2.D2
  N5: WeMos_D1_Mini2.D0, WeMos_D1_Mini2.RST

custom parts:
  BME280 Breakout: SparkFun Atmospheric Sensor Breakout - BME280 SEN-13676 The SparkFun BME280 Atmospheric Sensor Breakout is the easy way to measure barometric pressure, humidity, and temperature readings all without taking up too much space. Basically, anything you need to know about atmospheric conditions you can find out from this tiny breakout. The BME280 Breakout has been design to be used in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
